# Fritzing sketch sabr (saved by Fritzing 0.9.3b)

parts:
  Mod1 = TMC2209 [package=THT]
  M2 = Stepper Motor - Bipolar
  BAT1 = Lithium Ion Polymer Battery 11.1v 5000mah
  C4 = Capacitor Polarized [package=cpol-radial-100uf-25v]
  U1 = ESP32-38PinWide [part_number=ESP32-38PinWide]
  Part1 = InvenSense MPU6050
  Mod2 = TMC2209 [package=THT]
  M3 = Stepper Motor - Bipolar
  M4 = RioRand LM2596
  U3 = SWITCH-SPST-2 [package=switch-spst-vertical]
  A1 = battery capcity indicator module 1s-8s [package=THT]

nets:
  GND: Mod1.GND, Mod1.EN, BAT1.negative, C4.-, U1.GND, Part1.GND, Mod2.GND, Mod2.MS1, Mod2.EN, M4.Pin_4, A1.pin2
  VDD: Mod1.VDD, U1.3.3, Part1.VCC, Mod2.VDD
  N1: Mod1.B2, M2.D
  N2: Mod1.B1, M2.B
  N3: Mod1.A1, M2.C
  N4: Mod1.A2, M2.A
  N5: Mod1.VM, C4.+, Mod2.VM, M4.Pin_3, U3.P
  N6: Mod1.Dir, U1.GPIO18
  N7: Mod1.Step, U1.GPIO19
  N8: BAT1.positive, U3.O, A1.pin1
  N9: U1.GPIO11, M4.Pin_2
  N10: U1.VIN, M4.Pin_1
  N11: U1.GPIO17, Mod2.Dir
  N12: U1.GPIO5, Mod2.Step
  N13: U1.GPIO21, Part1.SDA
  N14: U1.GPIO22, Part1.SCL
  N15: Mod2.B2, M3.D
  N16: Mod2.B1, M3.B
  N17: Mod2.A1, M3.C
  N18: Mod2.A2, M3.A

custom parts:
  TMC2209: TMC2209-LA stepper motor controller and driver. Supply voltage 4.75-28V Iphase up to 1.77A rms (2.5A peak)
  ESP32-38PinWide: Generic 38-Pin ESP32 with wide format (only access to one side of pins on a breadboard) based on Stephen Lilley's HiLetgo ESP-WROOM-32 ESP32 ESP-32S Development Board.
  battery capcity indicator module 1s-8s: battery capcity indicator module 1s-8s.
